// Logisim project flipflops.circ as structural Verilog: 1 circuit, main circuit main
module main (
  input  [5:0] in_1,
  input  [8:0] in_2,
  input  in_3,
  input  [15:0] in_4,
  input  in_5,
  input  [15:0] in_6,
  input  [15:0] in_7,
  input  [15:0] in_8,
  input  [15:0] in_9,
  input  [15:0] in_10,
  input  in_11,
  input  in_12,
  input  in_13,
  input  in_14,
  input  [15:0] in_15,
  input  [2:0] in_16,
  input  [5:0] in_17,
  input  [8:0] in_18,
  input  in_19,
  input  in_20,
  input  in_21,
  input  [15:0] in_22,
  input  in_23,
  input  load,
  input  Reset,
  input  [2:0] in_26,
  input  in_27,
  input  [15:0] in_28
);

  wire clock_1_out, clock_2_out, clock_3_out, clock_4_out, clock_5_out, clock_6_out, clock_7_out,
       clock_8_out, clock_9_out, clock_10_out, clock_11_out, clock_12_out, clock_13_out, clock_14_out,
       d_ff_1_q, demultiplexer_1_out0, demultiplexer_1_out1, demultiplexer_1_out2, demultiplexer_1_out3,
       demultiplexer_1_out4, demultiplexer_1_out5, demultiplexer_1_out6, demultiplexer_1_out7,
       demultiplexer_2_out0, demultiplexer_2_out1, demultiplexer_2_out2, demultiplexer_2_out3,
       demultiplexer_2_out4, demultiplexer_2_out5, demultiplexer_2_out6, demultiplexer_2_out7,
       demultiplexer_3_out0, demultiplexer_3_out1, demultiplexer_3_out2, demultiplexer_3_out3,
       demultiplexer_3_out4, demultiplexer_3_out5, demultiplexer_3_out6, demultiplexer_3_out7,
       dipswitch_1_p1, dipswitch_2_p1, dipswitch_2_p2, dipswitch_3_p1, multiplexer_1_out, nand_1_out,
       nand_2_out, nand_3_out, nand_4_out, nand_5_out, nand_6_out, nand_8_out, nand_9_out, nand_10_out,
       nand_11_out, nand_12_out, not_1_out, not_2_out, not_3_out, not_4_out, or_1_out, or_2_out,
       register_1_q, register_3_q, register_4_q, register_5_q, register_6_q, register_7_q, register_8_q,
       register_9_q, register_10_q, register_11_q, register_12_q, register_13_q, register_14_q,
       register_15_q, register_16_q, register_17_q, register_18_q;
  wire [15:0] adder_1_out, adder_2_out, multiplexer_2_out, multiplexer_3_out, multiplexer_4_out,
       multiplexer_5_out, multiplexer_6_out, multiplexer_7_out, multiplexer_8_out, or_3_out, ram_1_dout,
       ram_2_dout, ram_3_dout, ram_4_dout, ram_5_dout, ram_6_dout, ram_7_dout, ram_8_dout, ram_9_dout,
       ram_10_dout, ram_11_dout, ram_12_dout, ram_13_dout, ram_14_dout, ram_15_dout, ram_16_dout,
       ram_17_dout, ram_18_dout, ram_19_dout, register_2_q, register_19_q, register_20_q, register_21_q,
       register_22_q, register_23_q, register_24_q, register_25_q, register_26_q, register_27_q,
       register_28_q;

  // DipSwitch #(.number(1)) dipswitch_1: pin names not known; wires that end beside it: dipswitch_1_p1
  Clock clock_1 (.out(clock_1_out));
  not not_1 (not_1_out, dipswitch_1_p1);
  // DipSwitch #(.number(2)) dipswitch_2: pin names not known; wires that end beside it: dipswitch_2_p1, dipswitch_2_p2
  nand nand_1 (nand_1_out, dipswitch_1_p1, clock_1_out);
  nand nand_2 (nand_2_out, clock_1_out, not_1_out);
  Multiplexer multiplexer_1 (.in0(d_ff_1_q), .in1(dipswitch_2_p1), .out(multiplexer_1_out), .sel(dipswitch_2_p2));
  Clock clock_2 (.out(clock_2_out));
  Register #(.width(1)) register_1 (
    .D(dipswitch_2_p1), .en(dipswitch_2_p2), .clk(clock_3_out), .Q(register_1_q));  // open: clr
  Clock clock_3 (.out(clock_3_out));
  D_Flip_Flop d_ff_1 (.D(multiplexer_1_out), .clk(clock_2_out), .Q(d_ff_1_q));  // open: Qn, preset, reset
  nand nand_3 (nand_3_out, nand_1_out, nand_4_out);
  nand nand_4 (nand_4_out, nand_2_out, nand_3_out);
  LED led_1 (.in(register_1_q));
  LED led_2 (.in(d_ff_1_q));
  Register #(.width(16)) register_2 (.D(in_10), .en(in_11), .clk(clock_4_out), .Q(register_2_q));  // open: clr
  Clock clock_4 (.out(clock_4_out));
  Clock clock_5 (.out(clock_5_out));
  Register #(.width(1)) register_3 (.D(in_10[0]), .en(in_11), .clk(clock_5_out), .Q(register_3_q));  // open: clr
  Register #(.width(1)) register_4 (.D(in_10[1]), .en(in_11), .clk(clock_5_out), .Q(register_4_q));  // open: clr
  Register #(.width(1)) register_5 (.D(in_10[2]), .en(in_11), .clk(clock_5_out), .Q(register_5_q));  // open: clr
  Register #(.width(1)) register_6 (.D(in_10[3]), .en(in_11), .clk(clock_5_out), .Q(register_6_q));  // open: clr
  Register #(.width(1)) register_7 (.D(in_10[4]), .en(in_11), .clk(clock_5_out), .Q(register_7_q));  // open: clr
  Register #(.width(1)) register_8 (.D(in_10[5]), .en(in_11), .clk(clock_5_out), .Q(register_8_q));  // open: clr
  Register #(.width(1)) register_9 (.D(in_10[6]), .en(in_11), .clk(clock_5_out), .Q(register_9_q));  // open: clr
  Register #(.width(1)) register_10 (.D(in_10[7]), .en(in_11), .clk(clock_5_out), .Q(register_10_q));  // open: clr
  Register #(.width(1)) register_11 (.D(in_10[8]), .en(in_11), .clk(clock_5_out), .Q(register_11_q));  // open: clr
  Register #(.width(1)) register_12 (.D(in_10[9]), .en(in_11), .clk(clock_5_out), .Q(register_12_q));  // open: clr
  Register #(.width(1)) register_13 (.D(in_10[10]), .en(in_11), .clk(clock_5_out), .Q(register_13_q));  // open: clr
  Register #(.width(1)) register_14 (.D(in_10[11]), .en(in_11), .clk(clock_5_out), .Q(register_14_q));  // open: clr
  Register #(.width(1)) register_15 (.D(in_10[12]), .en(in_11), .clk(clock_5_out), .Q(register_15_q));  // open: clr
  Register #(.width(1)) register_16 (.D(in_10[13]), .en(in_11), .clk(clock_5_out), .Q(register_16_q));  // open: clr
  Register #(.width(1)) register_17 (.D(in_10[14]), .en(in_11), .clk(clock_5_out), .Q(register_17_q));  // open: clr
  Register #(.width(1)) register_18 (.D(in_10[15]), .en(in_11), .clk(clock_5_out), .Q(register_18_q));  // open: clr
  LED led_3 (.in(nand_3_out));
  LED led_4 (.in(nand_4_out));
  LedBar #(.matrixcols(16)) ledbar_1 (
    .led0(register_2_q[15]), .led1(register_2_q[14]), .led2(register_2_q[13]), .led3(register_2_q[12]),
    .led4(register_2_q[11]), .led5(register_2_q[10]), .led6(register_2_q[9]), .led7(register_2_q[8]),
    .led8(register_2_q[7]), .led9(register_2_q[6]), .led10(register_2_q[5]), .led11(register_2_q[4]),
    .led12(register_2_q[3]), .led13(register_2_q[2]), .led14(register_2_q[1]), .led15(register_2_q[0]));
  LED led_5 (.in(register_3_q));
  LED led_6 (.in(register_4_q));
  LED led_7 (.in(register_5_q));
  LED led_8 (.in(register_6_q));
  LED led_9 (.in(register_7_q));
  LED led_10 (.in(register_8_q));
  LED led_11 (.in(register_9_q));
  LED led_12 (.in(register_10_q));
  LED led_13 (.in(register_11_q));
  LED led_14 (.in(register_12_q));
  LED led_15 (.in(register_13_q));
  LED led_16 (.in(register_14_q));
  LED led_17 (.in(register_15_q));
  LED led_18 (.in(register_16_q));
  LED led_19 (.in(register_17_q));
  LED led_20 (.in(register_18_q));
  // DipSwitch #(.number(1)) dipswitch_3: pin names not known; wires that end beside it: dipswitch_3_p1
  Clock clock_6 (.out(clock_6_out));
  not not_2 (not_2_out, clock_6_out);
  not not_3 (not_3_out, dipswitch_3_p1);
  nand nand_5 (nand_5_out, dipswitch_3_p1, clock_6_out);
  nand nand_6 (nand_6_out, clock_6_out, not_3_out);
  nand nand_7 (not_2_out, nand_5_out, nand_8_out);
  nand nand_8 (nand_8_out, not_2_out, nand_6_out);
  LED led_21 (.in(nand_8_out));
  Demultiplexer #(.select(3)) demultiplexer_1 (
    .out0(demultiplexer_1_out0), .out1(demultiplexer_1_out1), .out2(demultiplexer_1_out2),
    .out3(demultiplexer_1_out3), .out4(demultiplexer_1_out4), .out5(demultiplexer_1_out5),
    .out6(demultiplexer_1_out6), .out7(demultiplexer_1_out7), .in(in_13), .sel(in_16));
  not not_4 (not_4_out, not_2_out);
  RAM #(.addrWidth(3), .dataWidth(16)) ram_1 (
    .addr(in_26), .we(in_27), .clk(clock_7_out), .din(in_28), .dout(ram_1_dout));  // open: oe
  Clock clock_7 (.out(clock_7_out));
  nand nand_9 (nand_9_out, not_2_out, not_2_out);
  nand nand_10 (nand_10_out, not_2_out, not_4_out);
  Clock clock_8 (.out(clock_8_out));
  nand nand_11 (nand_11_out, nand_9_out, nand_12_out);
  nand nand_12 (nand_12_out, nand_11_out, nand_10_out);
  Register #(.width(16)) register_19 (
    .D(in_9), .en(demultiplexer_1_out0), .clk(clock_8_out), .Q(register_19_q));  // open: clr
  Register #(.width(16)) register_20 (
    .D(in_9), .en(demultiplexer_1_out1), .clk(clock_8_out), .Q(register_20_q));  // open: clr
  Register #(.width(16)) register_21 (
    .D(in_9), .en(demultiplexer_1_out2), .clk(clock_8_out), .Q(register_21_q));  // open: clr
  Register #(.width(16)) register_22 (
    .D(in_9), .en(demultiplexer_1_out3), .clk(clock_8_out), .Q(register_22_q));  // open: clr
  Register #(.width(16)) register_23 (
    .D(in_9), .en(demultiplexer_1_out4), .clk(clock_8_out), .Q(register_23_q));  // open: clr
  Register #(.width(16)) register_24 (
    .D(in_9), .en(demultiplexer_1_out5), .clk(clock_8_out), .Q(register_24_q));  // open: clr
  Register #(.width(16)) register_25 (
    .D(in_9), .en(demultiplexer_1_out6), .clk(clock_8_out), .Q(register_25_q));  // open: clr
  Register #(.width(16)) register_26 (
    .D(in_9), .en(demultiplexer_1_out7), .clk(clock_8_out), .Q(register_26_q));  // open: clr
  LED led_22 (.in(nand_11_out));
  LED led_23 (.in(nand_12_out));
  // LedBar #(.inputtype("row"), .matrixcols(16)) ledbar_2: pin names not known; wires that end beside it: ram_1_dout
  Multiplexer #(.select(3), .width(16)) multiplexer_2 (
    .in0(register_19_q), .in1(register_20_q), .in2(register_21_q), .in3(register_22_q), .in4(register_23_q),
    .in5(register_24_q), .in6(register_25_q), .in7(register_26_q), .out(multiplexer_2_out), .sel(in_16));
  LedBar #(.matrixcols(16)) ledbar_3 (
    .led0(multiplexer_2_out[15]), .led1(multiplexer_2_out[14]), .led2(multiplexer_2_out[13]),
    .led3(multiplexer_2_out[12]), .led4(multiplexer_2_out[11]), .led5(multiplexer_2_out[10]),
    .led6(multiplexer_2_out[9]), .led7(multiplexer_2_out[8]), .led8(multiplexer_2_out[7]),
    .led9(multiplexer_2_out[6]), .led10(multiplexer_2_out[5]), .led11(multiplexer_2_out[4]),
    .led12(multiplexer_2_out[3]), .led13(multiplexer_2_out[2]), .led14(multiplexer_2_out[1]),
    .led15(multiplexer_2_out[0]));
  Demultiplexer #(.select(3)) demultiplexer_2 (
    .out0(demultiplexer_2_out0), .out1(demultiplexer_2_out1), .out2(demultiplexer_2_out2),
    .out3(demultiplexer_2_out3), .out4(demultiplexer_2_out4), .out5(demultiplexer_2_out5),
    .out6(demultiplexer_2_out6), .out7(demultiplexer_2_out7), .in(in_12), .sel(in_17[5:3]));
  RAM #(.addrWidth(6), .dataWidth(16)) ram_2 (
    .addr(in_1), .we(in_3), .clk(clock_9_out), .din(in_4), .dout(ram_2_dout));  // open: oe
  Clock clock_9 (.out(clock_9_out));
  RAM #(.addrWidth(3), .dataWidth(16)) ram_3 (
    .addr(in_17[2:0]), .we(demultiplexer_2_out0), .clk(clock_10_out), .din(in_7), .dout(ram_3_dout));  // open: oe
  RAM #(.addrWidth(3), .dataWidth(16)) ram_4 (
    .addr(in_17[2:0]), .we(demultiplexer_2_out1), .clk(clock_10_out), .din(in_7), .dout(ram_4_dout));  // open: oe
  RAM #(.addrWidth(3), .dataWidth(16)) ram_5 (
    .addr(in_17[2:0]), .we(demultiplexer_2_out2), .clk(clock_10_out), .din(in_7), .dout(ram_5_dout));  // open: oe
  RAM #(.addrWidth(3), .dataWidth(16)) ram_6 (
    .addr(in_17[2:0]), .we(demultiplexer_2_out3), .clk(clock_10_out), .din(in_7), .dout(ram_6_dout));  // open: oe
  Clock clock_10 (.out(clock_10_out));
  // LedBar #(.inputtype("row"), .matrixcols(16)) ledbar_4: pin names not known; wires that end beside it: ram_2_dout
  RAM #(.addrWidth(3), .dataWidth(16)) ram_7 (
    .addr(in_17[2:0]), .we(demultiplexer_2_out4), .clk(clock_10_out), .din(in_7), .dout(ram_7_dout));  // open: oe
  RAM #(.addrWidth(3), .dataWidth(16)) ram_8 (
    .addr(in_17[2:0]), .we(demultiplexer_2_out5), .clk(clock_10_out), .din(in_7), .dout(ram_8_dout));  // open: oe
  RAM #(.addrWidth(3), .dataWidth(16)) ram_9 (
    .addr(in_17[2:0]), .we(demultiplexer_2_out6), .clk(clock_10_out), .din(in_7), .dout(ram_9_dout));  // open: oe
  RAM #(.addrWidth(3), .dataWidth(16)) ram_10 (
    .addr(in_17[2:0]), .we(demultiplexer_2_out7), .clk(clock_10_out), .din(in_7), .dout(ram_10_dout));  // open: oe
  Multiplexer #(.select(3), .width(16)) multiplexer_3 (
    .in0(ram_3_dout), .in1(ram_4_dout), .in2(ram_5_dout), .in3(ram_6_dout), .in4(ram_7_dout),
    .in5(ram_8_dout), .in6(ram_9_dout), .in7(ram_10_dout), .out(multiplexer_3_out), .sel(in_17[5:3]));
  // LedBar #(.inputtype("row"), .matrixcols(16)) ledbar_5: pin names not known; wires that end beside it: multiplexer_3_out
  Demultiplexer #(.select(3)) demultiplexer_3 (
    .out0(demultiplexer_3_out0), .out1(demultiplexer_3_out1), .out2(demultiplexer_3_out2),
    .out3(demultiplexer_3_out3), .out4(demultiplexer_3_out4), .out5(demultiplexer_3_out5),
    .out6(demultiplexer_3_out6), .out7(demultiplexer_3_out7), .in(in_14), .sel(in_18[8:6]));
  RAM #(.addrWidth(9), .dataWidth(16)) ram_11 (
    .addr(in_2), .we(in_5), .clk(clock_11_out), .din(in_6), .dout(ram_11_dout));  // open: oe
  Clock clock_11 (.out(clock_11_out));
  RAM #(.addrWidth(6), .dataWidth(16)) ram_12 (
    .addr({in_18[2:0], in_18[5:3]}), .we(demultiplexer_3_out0), .clk(clock_12_out), .din(in_8),
    .dout(ram_12_dout));  // open: oe
  RAM #(.addrWidth(6), .dataWidth(16)) ram_13 (
    .addr({in_18[2:0], in_18[5:3]}), .we(demultiplexer_3_out1), .clk(clock_12_out), .din(in_8),
    .dout(ram_13_dout));  // open: oe
  RAM #(.addrWidth(6), .dataWidth(16)) ram_14 (
    .addr({in_18[2:0], in_18[5:3]}), .we(demultiplexer_3_out2), .clk(clock_12_out), .din(in_8),
    .dout(ram_14_dout));  // open: oe
  RAM #(.addrWidth(6), .dataWidth(16)) ram_15 (
    .addr({in_18[2:0], in_18[5:3]}), .we(demultiplexer_3_out3), .clk(clock_12_out), .din(in_8),
    .dout(ram_15_dout));  // open: oe
  // LedBar #(.inputtype("row"), .matrixcols(16)) ledbar_6: pin names not known; wires that end beside it: ram_11_dout
  Clock clock_12 (.out(clock_12_out));
  Multiplexer #(.select(3), .width(16)) multiplexer_4 (
    .in0(ram_12_dout), .in1(ram_13_dout), .in2(ram_14_dout), .in3(ram_15_dout), .in4(ram_16_dout),
    .in5(ram_17_dout), .in6(ram_18_dout), .in7(ram_19_dout), .out(multiplexer_4_out), .sel(in_18[8:6]));
  RAM #(.addrWidth(6), .dataWidth(16)) ram_16 (
    .addr({in_18[2:0], in_18[5:3]}), .we(demultiplexer_3_out4), .clk(clock_12_out), .din(in_8),
    .dout(ram_16_dout));  // open: oe
  RAM #(.addrWidth(6), .dataWidth(16)) ram_17 (
    .addr({in_18[2:0], in_18[5:3]}), .we(demultiplexer_3_out5), .clk(clock_12_out), .din(in_8),
    .dout(ram_17_dout));  // open: oe
  RAM #(.addrWidth(6), .dataWidth(16)) ram_18 (
    .addr({in_18[2:0], in_18[5:3]}), .we(demultiplexer_3_out6), .clk(clock_12_out), .din(in_8),
    .dout(ram_18_dout));  // open: oe
  RAM #(.addrWidth(6), .dataWidth(16)) ram_19 (
    .addr({in_18[2:0], in_18[5:3]}), .we(demultiplexer_3_out7), .clk(clock_12_out), .din(in_8),
    .dout(ram_19_dout));  // open: oe
  // LedBar #(.inputtype("row"), .matrixcols(16)) ledbar_7: pin names not known; wires that end beside it: multiplexer_4_out
  Counter counter_1 ();  // open: clr, load, up, count, clk, D, carry, Q
  Adder #(.width(16)) adder_1 (.a(16'h1), .b(register_27_q), .out(adder_1_out));  // open: cin, cout
  Adder #(.width(16)) adder_2 (.a(16'h1), .b(register_28_q), .out(adder_2_out));  // open: cin, cout
  Multiplexer #(.select(3), .width(16)) multiplexer_5 (
    .in0(register_27_q), .in1(adder_1_out), .in2(in_15), .in3(in_15), .in4({16{1'b0}}), .in5({16{1'b0}}),
    .in6({16{1'b0}}), .in7({16{1'b0}}), .out(multiplexer_5_out), .sel({in_21, in_20, in_19}));
  Register #(.width(16)) register_27 (
    .D(multiplexer_5_out), .en(1'b1), .clk(clock_13_out), .Q(register_27_q));  // open: clr
  Clock clock_13 (.out(clock_13_out));
  Multiplexer #(.width(16)) multiplexer_6 (
    .in0(register_28_q), .in1(adder_2_out), .out(multiplexer_6_out), .sel(in_23));
  Multiplexer #(.width(16)) multiplexer_7 (.in0(multiplexer_6_out), .in1(in_22), .out(multiplexer_7_out), .sel(load));
  Multiplexer #(.width(16)) multiplexer_8 (
    .in0(multiplexer_7_out), .in1({16{1'b0}}), .out(multiplexer_8_out), .sel(Reset));
  or or_1 (or_1_out, in_23, load);
  Hex_Digit_Display hex_digit_display_1 (.value(register_27_q[15:12]));  // open: dp
  Hex_Digit_Display hex_digit_display_2 (.value(register_27_q[11:8]));  // open: dp
  or or_2 (or_2_out, or_1_out, Reset);
  Hex_Digit_Display hex_digit_display_3 (.value(register_27_q[7:4]));  // open: dp
  Hex_Digit_Display hex_digit_display_4 (.value(register_27_q[3:0]));  // open: dp
  Register #(.width(16)) register_28 (
    .D(multiplexer_8_out), .en(or_2_out), .clk(clock_14_out), .Q(register_28_q));  // open: clr
  Clock clock_14 (.out(clock_14_out));
  assign or_3_out = register_28_q | register_28_q;  // OR_Gate or_3, 16 bits wide
  Hex_Digit_Display hex_digit_display_5 (.value(or_3_out[15:12]));  // open: dp
  Hex_Digit_Display hex_digit_display_6 (.value(or_3_out[11:8]));  // open: dp
  Hex_Digit_Display hex_digit_display_7 (.value(or_3_out[7:4]));  // open: dp
  Hex_Digit_Display hex_digit_display_8 (.value(or_3_out[3:0]));  // open: dp

  // Notes on the sheet:
  //   sw1 = d
  //   clock = e
  //   gated d-latch
  //   1 bit register
  //   16 bit register
  //   MS-D flip flop
  //   RAM 8
  //   16 bit 8 registers
  //   RAM 64
  //   16 bit 64 registers
  //   RAM 512
  //   16 bit 512 registers
  //   Incrementer
endmodule
