// Logisim project circuits.circ as structural Verilog: 1 circuit, main circuit main
module main (
  input  [15:0] in_1,
  input  [15:0] in_2,
  input  [15:0] in_3,
  input  in_4,
  input  in_5,
  input  [14:0] in_6,
  input  [15:0] in_7,
  input  [15:0] in_8,
  input  res,
  input  [15:0] in_10,
  input  reset,
  input  load,
  input  incr
);

  wire and_1_out, and_2_out, and_3_out, and_4_out, and_5_out, and_10_out, and_11_out, and_12_out, and_13_out,
       and_14_out, clock_1_out, clock_2_out, clock_3_out, clock_4_out, clock_5_out, clock_6_out,
       demultiplexer_1_out0, demultiplexer_1_out1, demultiplexer_2_out0, demultiplexer_2_out1, ledbar_9_p1,
       ledbar_15_p1, not_1_out, not_2_out, not_11_out, not_12_out, not_15_out, not_16_out, not_18_out,
       or_1_out, or_2_out, or_5_out, or_6_out, or_7_out, or_8_out, or_9_out, or_10_out, or_11_out, or_12_out,
       or_13_out, or_14_out, or_15_out, or_16_out, or_17_out, or_18_out, or_19_out, or_20_out, or_21_out,
       or_22_out, or_23_out, or_24_out, or_25_out, or_26_out, or_27_out, or_28_out, or_29_out, or_30_out,
       or_31_out, or_32_out, or_33_out, or_34_out, or_35_out, or_36_out, or_37_out, or_38_out, or_39_out,
       or_40_out, or_41_out, or_42_out, or_43_out, or_44_out, or_45_out, or_46_out, or_47_out, or_48_out,
       or_49_out, or_50_out, or_51_out, or_52_out, or_53_out, or_54_out, undriven_2, undriven_3, undriven_4,
       undriven_5, undriven_6, undriven_9, undriven_10, undriven_11, undriven_12, undriven_13;
  wire [15:0] adder_1_out, adder_2_out, adder_3_out, adder_4_out, and_7_out, and_8_out, and_9_out,
       counter_1_q, ledbar_4_p1, ledbar_6_p1, multiplexer_1_out, multiplexer_2_out, multiplexer_3_out,
       multiplexer_4_out, multiplexer_5_out, multiplexer_6_out, multiplexer_7_out, multiplexer_8_out,
       multiplexer_9_out, multiplexer_10_out, multiplexer_11_out, multiplexer_12_out, multiplexer_13_out,
       multiplexer_14_out, multiplexer_15_out, multiplexer_16_out, multiplexer_18_out, multiplexer_19_out,
       multiplexer_20_out, multiplexer_21_out, multiplexer_22_out, multiplexer_23_out, multiplexer_24_out,
       not_3_out, not_4_out, not_7_out, not_8_out, not_9_out, not_10_out, not_13_out, not_14_out, not_17_out,
       ram_1_dout, ram_2_dout, register_1_q, register_2_q, register_3_q, register_5_q, register_6_q,
       undriven, undriven_7, undriven_8;

  Demultiplexer demultiplexer_1 (.out0(demultiplexer_1_out0), .out1(demultiplexer_1_out1), .in(in_4), .sel(in_6[14]));
  Demultiplexer demultiplexer_2 (
    .out0(demultiplexer_2_out0), .out1(demultiplexer_2_out1), .in(demultiplexer_1_out1), .sel(in_6[13]));
  RAM #(.addrWidth(14), .dataWidth(16)) ram_1 (
    .addr(in_6[13:0]), .we(demultiplexer_1_out0), .clk(clock_1_out), .din(in_1), .dout(ram_1_dout));  // open: oe
  Clock clock_1 (.out(clock_1_out));
  // LedBar #(.inputtype("row"), .matrixcols(16)) ledbar_1: pin names not known; wires that end beside it: ram_1_dout
  Register #(.width(16)) register_1 (.clk(clock_2_out), .Q(register_1_q));  // open: D, en, clr
  Clock clock_2 (.out(clock_2_out));
  Clock clock_3 (.out(clock_3_out));
  RAM #(.addrWidth(13), .dataWidth(16)) ram_2 (
    .addr(in_6[12:0]), .we(demultiplexer_2_out0), .clk(clock_3_out), .din(in_1), .dout(ram_2_dout));  // open: oe
  Multiplexer #(.width(16)) multiplexer_1 (
    .in0(ram_2_dout), .in1(register_1_q), .out(multiplexer_1_out), .sel(in_6[13]));
  Multiplexer #(.width(16)) multiplexer_2 (
    .in0(ram_1_dout), .in1(multiplexer_1_out), .out(multiplexer_2_out), .sel(in_6[14]));
  // LedBar #(.inputtype("row"), .matrixcols(16)) ledbar_2: pin names not known; wires that end beside it: multiplexer_2_out
  // LedBar #(.inputtype("row"), .matrixcols(16)) ledbar_3: pin names not known; wires that end beside it: ram_2_dout
  not not_1 (not_1_out, undriven[15]);
  Clock clock_4 (.out(clock_4_out));
  not not_2 (not_2_out, in_7[15]);
  and and_1 (and_1_out, undriven[15], undriven[5]);
  and and_2 (and_2_out, undriven[15], undriven[4]);
  Multiplexer #(.width(16)) multiplexer_3 (
    .in0(multiplexer_13_out), .in1(undriven), .out(multiplexer_3_out), .sel(not_1_out));
  and and_3 (and_3_out, in_7[15], in_7[3]);
  Register #(.width(16)) register_2 (
    .D(multiplexer_3_out), .en(or_1_out), .clk(clock_5_out), .Q(register_2_q));  // open: clr
  Clock clock_5 (.out(clock_5_out));
  or or_1 (or_1_out, and_1_out, not_1_out);
  Multiplexer #(.width(16)) multiplexer_4 (.in0(ledbar_4_p1), .in1(in_7), .out(multiplexer_4_out), .sel(not_2_out));
  Register #(.width(16)) register_3 (.D(register_2_q), .en(and_2_out), .clk(clock_5_out), .Q(register_3_q), .clr(in_5));
  // LedBar #(.inputtype("row"), .matrixcols(16)) ledbar_4: pin names not known; wires that end beside it: ledbar_4_p1
  // LedBar #(.inputtype("row"), .matrixcols(1)) ledbar_5: pin names not known; wires that end beside it: and_3_out
  // LedBar #(.inputtype("row"), .matrixcols(15)) ledbar_6: pin names not known; wires that end beside it: ledbar_6_p1[14:0]
  // LedBar #(.inputtype("row"), .matrixcols(15)) ledbar_7: pin names not known
  and and_4 (and_4_out, in_7[15], in_7[5]);
  // LedBar #(.inputtype("row"), .matrixcols(16)) ledbar_8: pin names not known; wires that end beside it: register_2_q
  Register #(.width(16)) register_4 (
    .D(multiplexer_4_out), .en(or_2_out), .clk(clock_4_out), .Q(ledbar_6_p1), .clr(res));
  or or_2 (or_2_out, and_4_out, not_2_out);
  and and_5 (and_5_out, in_7[15], in_7[4]);
  Register #(.width(16)) register_5 (.D(ledbar_4_p1), .en(and_5_out), .clk(clock_4_out), .Q(register_5_q), .clr(res));
  Multiplexer #(.width(16)) multiplexer_5 (
    .in0(register_3_q), .in1({16{1'b0}}), .out(multiplexer_5_out), .sel(undriven_2));
  Multiplexer #(.width(16)) multiplexer_6 (
    .in0(multiplexer_3_out), .in1({16{1'b0}}), .out(multiplexer_6_out), .sel(undriven_3));
  Multiplexer #(.width(16)) multiplexer_7 (
    .in0(multiplexer_5_out), .in1(not_3_out), .out(multiplexer_7_out), .sel(undriven_4));
  assign not_3_out = ~multiplexer_5_out;  // NOT_Gate not_3, 16 bits wide
  Multiplexer #(.width(16)) multiplexer_8 (
    .in0(multiplexer_6_out), .in1(not_4_out), .out(multiplexer_8_out), .sel(undriven_5));
  assign not_4_out = ~multiplexer_6_out;  // NOT_Gate not_4, 16 bits wide
  // AND_Gate and_6 is placed but not wired
  // OR_Gate or_3 is placed but not wired
  // OR_Gate or_4 is placed but not wired
  // NOT_Gate not_5 is placed but not wired
  // NOT_Gate not_6 is placed but not wired
  assign and_7_out = multiplexer_7_out & multiplexer_8_out;  // AND_Gate and_7, 16 bits wide
  Adder #(.width(16)) adder_1 (.a(multiplexer_8_out), .b(multiplexer_7_out), .out(adder_1_out));  // open: cin, cout
  Multiplexer #(.width(16)) multiplexer_9 (
    .in0(and_7_out), .in1(adder_1_out), .out(multiplexer_9_out), .sel(undriven_6));
  Multiplexer #(.width(16)) multiplexer_10 (.in0(ledbar_6_p1), .in1(in_8), .out(multiplexer_10_out), .sel(in_7[12]));
  assign not_7_out = ~multiplexer_9_out;  // NOT_Gate not_7, 16 bits wide
  Multiplexer #(.width(16)) multiplexer_11 (
    .in0(register_5_q), .in1({16{1'b0}}), .out(multiplexer_11_out), .sel(in_7[11]));
  Multiplexer #(.width(16)) multiplexer_12 (
    .in0(multiplexer_10_out), .in1({16{1'b0}}), .out(multiplexer_12_out), .sel(in_7[9]));
  Multiplexer #(.width(16)) multiplexer_13 (
    .in0(multiplexer_9_out), .in1(not_7_out), .out(multiplexer_13_out), .sel(ledbar_9_p1));
  // LedBar #(.inputtype("row"), .matrixcols(16)) ledbar_9: pin names not known; wires that end beside it: ledbar_9_p1, multiplexer_13_out
  Multiplexer #(.width(16)) multiplexer_14 (
    .in0(multiplexer_11_out), .in1(not_8_out), .out(multiplexer_14_out), .sel(in_7[10]));
  assign not_8_out = ~multiplexer_11_out;  // NOT_Gate not_8, 16 bits wide
  Multiplexer #(.width(16)) multiplexer_15 (
    .in0(multiplexer_12_out), .in1(not_9_out), .out(multiplexer_15_out), .sel(in_7[8]));
  assign not_9_out = ~multiplexer_12_out;  // NOT_Gate not_9, 16 bits wide
  or or_5 (or_5_out, multiplexer_13_out[15], 1'b0);
  LED led_1 (.in(or_5_out));
  or or_6 (or_6_out, multiplexer_13_out[0], multiplexer_13_out[1]);
  or or_7 (or_7_out, multiplexer_13_out[8], multiplexer_13_out[9]);
  assign and_8_out = multiplexer_14_out & multiplexer_15_out;  // AND_Gate and_8, 16 bits wide
  Adder #(.width(16)) adder_2 (.a(multiplexer_15_out), .b(multiplexer_14_out), .out(adder_2_out));  // open: cin, cout
  // LedBar #(.inputtype("row"), .matrixcols(16)) ledbar_10: pin names not known; wires that end beside it: multiplexer_13_out
  // LedBar #(.inputtype("row"), .matrixcols(1)) ledbar_11: pin names not known
  // LedBar #(.inputtype("row"), .matrixcols(15)) ledbar_12: pin names not known
  // LedBar #(.inputtype("row"), .matrixcols(15)) ledbar_13: pin names not known
  or or_8 (or_8_out, or_6_out, multiplexer_13_out[2]);
  or or_9 (or_9_out, or_7_out, multiplexer_13_out[10]);
  Multiplexer #(.width(16)) multiplexer_16 (
    .in0(and_8_out), .in1(adder_2_out), .out(multiplexer_16_out), .sel(in_7[7]));
  or or_10 (or_10_out, or_8_out, multiplexer_13_out[3]);
  or or_11 (or_11_out, or_9_out, multiplexer_13_out[11]);
  or or_12 (or_12_out, or_11_out, multiplexer_13_out[12]);
  assign not_10_out = ~multiplexer_16_out;  // NOT_Gate not_10, 16 bits wide
  or or_13 (or_13_out, or_10_out, multiplexer_13_out[4]);
  or or_14 (or_14_out, or_13_out, multiplexer_13_out[5]);
  or or_15 (or_15_out, or_12_out, multiplexer_13_out[13]);
  Multiplexer #(.width(16)) multiplexer_17 (
    .in0(multiplexer_16_out), .in1(not_10_out), .out(ledbar_4_p1), .sel(in_7[6]));
  or or_16 (or_16_out, or_14_out, multiplexer_13_out[6]);
  or or_17 (or_17_out, or_15_out, multiplexer_13_out[14]);
  // LedBar #(.inputtype("row"), .matrixcols(16)) ledbar_14: pin names not known; wires that end beside it: ledbar_4_p1
  or or_18 (or_18_out, or_16_out, multiplexer_13_out[7]);
  or or_19 (or_19_out, or_17_out, multiplexer_13_out[15]);
  or or_20 (or_20_out, ledbar_4_p1[15], 1'b0);
  LED led_2 (.in(or_20_out));
  or or_21 (or_21_out, or_18_out, or_19_out);
  or or_22 (or_22_out, ledbar_4_p1[0], ledbar_4_p1[1]);
  or or_23 (or_23_out, ledbar_4_p1[8], ledbar_4_p1[9]);
  not not_11 (not_11_out, or_20_out);
  not not_12 (not_12_out, or_21_out);
  LED led_3 (.in(not_12_out));
  or or_24 (or_24_out, or_22_out, ledbar_4_p1[2]);
  or or_25 (or_25_out, or_23_out, ledbar_4_p1[10]);
  or or_26 (or_26_out, or_24_out, ledbar_4_p1[3]);
  or or_27 (or_27_out, or_25_out, ledbar_4_p1[11]);
  or or_28 (or_28_out, or_27_out, ledbar_4_p1[12]);
  or or_29 (or_29_out, or_26_out, ledbar_4_p1[4]);
  or or_30 (or_30_out, or_29_out, ledbar_4_p1[5]);
  or or_31 (or_31_out, or_28_out, ledbar_4_p1[13]);
  or or_32 (or_32_out, or_30_out, ledbar_4_p1[6]);
  or or_33 (or_33_out, or_31_out, ledbar_4_p1[14]);
  Multiplexer #(.width(16)) multiplexer_18 (
    .in0(undriven_8), .in1({16{1'b0}}), .out(multiplexer_18_out), .sel(undriven_9));
  Multiplexer #(.width(16)) multiplexer_19 (
    .in0(undriven_7), .in1({16{1'b0}}), .out(multiplexer_19_out), .sel(undriven_10));
  or or_34 (or_34_out, or_32_out, ledbar_4_p1[7]);
  or or_35 (or_35_out, or_33_out, ledbar_4_p1[15]);
  assign not_13_out = ~multiplexer_18_out;  // NOT_Gate not_13, 16 bits wide
  assign not_14_out = ~multiplexer_19_out;  // NOT_Gate not_14, 16 bits wide
  or or_36 (or_36_out, or_34_out, or_35_out);
  not not_15 (not_15_out, or_36_out);
  Multiplexer #(.width(16)) multiplexer_20 (
    .in0(multiplexer_18_out), .in1(not_13_out), .out(multiplexer_20_out), .sel(undriven_11));
  Multiplexer #(.width(16)) multiplexer_21 (
    .in0(multiplexer_19_out), .in1(not_14_out), .out(multiplexer_21_out), .sel(undriven_12));
  LED led_4 (.in(not_15_out));
  not not_16 (not_16_out, not_15_out);
  assign and_9_out = multiplexer_20_out & multiplexer_21_out;  // AND_Gate and_9, 16 bits wide
  Adder #(.width(16)) adder_3 (.a(multiplexer_21_out), .b(multiplexer_20_out), .out(adder_3_out));  // open: cin, cout
  and and_10 (and_10_out, not_16_out, not_11_out);
  Multiplexer #(.width(16)) multiplexer_22 (
    .in0(and_9_out), .in1(adder_3_out), .out(multiplexer_22_out), .sel(undriven_13));
  Multiplexer #(.width(16)) multiplexer_23 (
    .in0(multiplexer_22_out), .in1(not_17_out), .out(multiplexer_23_out), .sel(ledbar_15_p1));
  assign not_17_out = ~multiplexer_22_out;  // NOT_Gate not_17, 16 bits wide
  and and_11 (and_11_out, in_7[2], or_20_out);
  and and_12 (and_12_out, in_7[1], or_36_out);
  and and_13 (and_13_out, in_7[0], and_10_out);
  // LedBar #(.inputtype("row"), .matrixcols(16)) ledbar_15: pin names not known; wires that end beside it: ledbar_15_p1, multiplexer_23_out
  or or_37 (or_37_out, multiplexer_23_out[15], 1'b0);
  or or_38 (or_38_out, and_11_out, and_12_out);
  LED led_5 (.in(or_37_out));
  or or_39 (or_39_out, or_38_out, and_13_out);
  or or_40 (or_40_out, multiplexer_23_out[0], multiplexer_23_out[1]);
  or or_41 (or_41_out, multiplexer_23_out[8], multiplexer_23_out[9]);
  or or_42 (or_42_out, or_41_out, multiplexer_23_out[10]);
  or or_43 (or_43_out, or_40_out, multiplexer_23_out[2]);
  or or_44 (or_44_out, or_43_out, multiplexer_23_out[3]);
  or or_45 (or_45_out, or_42_out, multiplexer_23_out[11]);
  and and_14 (and_14_out, or_39_out, in_7[15]);
  or or_46 (or_46_out, or_44_out, multiplexer_23_out[4]);
  or or_47 (or_47_out, or_45_out, multiplexer_23_out[12]);
  or or_48 (or_48_out, or_46_out, multiplexer_23_out[5]);
  or or_49 (or_49_out, or_47_out, multiplexer_23_out[13]);
  or or_50 (or_50_out, or_49_out, multiplexer_23_out[14]);
  or or_51 (or_51_out, or_48_out, multiplexer_23_out[6]);
  or or_52 (or_52_out, or_51_out, multiplexer_23_out[7]);
  or or_53 (or_53_out, or_50_out, multiplexer_23_out[15]);
  or or_54 (or_54_out, or_52_out, or_53_out);
  not not_18 (not_18_out, or_54_out);
  LED led_6 (.in(not_18_out));
  Counter #(.max('hffff), .width(16)) counter_1 (
    .clr(res), .load(and_14_out), .up(1'b1), .count(1'b1), .D(ledbar_4_p1), .Q(counter_1_q));  // open: clk, carry
  Hex_Digit_Display hex_digit_display_1 (.value(counter_1_q[15:12]));  // open: dp
  Hex_Digit_Display hex_digit_display_2 (.value(counter_1_q[11:8]));  // open: dp
  Hex_Digit_Display hex_digit_display_3 (.value(counter_1_q[7:4]));  // open: dp
  Hex_Digit_Display hex_digit_display_4 (.value(counter_1_q[3:0]));  // open: dp
  Adder #(.width(16)) adder_4 (.a(16'h1), .b(register_6_q), .out(adder_4_out));  // open: cin, cout
  Multiplexer #(.select(3), .width(16)) multiplexer_24 (
    .in0(register_6_q), .in1(adder_4_out), .in2(in_10), .in3(in_10), .in4({16{1'b0}}), .in5({16{1'b0}}),
    .in6({16{1'b0}}), .in7({16{1'b0}}), .out(multiplexer_24_out), .sel({incr, load, reset}));
  Register #(.width(16)) register_6 (
    .D(multiplexer_24_out), .en(1'b1), .clk(clock_6_out), .Q(register_6_q));  // open: clr
  Clock clock_6 (.out(clock_6_out));
  Hex_Digit_Display hex_digit_display_5 (.value(register_6_q[15:12]));  // open: dp
  Hex_Digit_Display hex_digit_display_6 (.value(register_6_q[11:8]));  // open: dp
  Hex_Digit_Display hex_digit_display_7 (.value(register_6_q[7:4]));  // open: dp
  Hex_Digit_Display hex_digit_display_8 (.value(register_6_q[3:0]));  // open: dp

  // Notes on the sheet:
  //   Memory
  //   This is RAM part
  //   Keyboard
  //   This denotes Screen
  //   ins
  //   inM
  //   isC
  //   clk
  //   isC
  //   isA
  //   A register
  //   isA
  //   D register
  //   A reg comp
  //   writeM
  //   outM
  //   addressM
  //   pc
  //   D reg comp
  //   Falied CPU
  //   CPU Architecture
  //   jmp and
  //   jmp or1
  //   jmp or2
  //   jmp not1
  //   jmp not2
  //   jmpIfNg
  //   JmpIfZr
  //   jmpIfPs
  //   jmpOr1
  //   shouldJmp
  //   doJmp
endmodule
